# Fritzing sketch Laser-Pong (saved by Fritzing 0.8.5b)
breadboards: 1

parts:
  Part1 = Arduino Prototyping Shield
  S1 = Pushbutton [package="[THT]"]
  S2 = Pushbutton [package="[THT]"]
  S3 = Pushbutton [package="[THT]"]
  R1 = Resistor [tolerance=±5% resistance=10k package=THT]
  R2 = Resistor [tolerance=±5% resistance=10k package=THT]
  R3 = Resistor [tolerance=±5% resistance=10k package=THT]
  J1 = Basic Servo
  7_Segment1 = 7 Segment Display
  7_Segment2 = 7 Segment Display
  7_Segment4 = 7 Segment Display
  7_Segment3 = 7 Segment Display

nets (from the schematic view):
  N1: Part1.A5, J1.pulse
  +5V: Part1.+5V, J1.vcc
  GND: Part1.GND, R1.Pin_1, R2.Pin_1, R3.Pin_1, J1.gnd
  N2: Part1.D8, S2.Pin_1, S2.Pin_2, R1.Pin_0
  N3: Part1.D10, S3.Pin_1, S3.Pin_2, R2.Pin_0
  N4: Part1.D11, S1.Pin_3, S1.Pin_4, S2.Pin_3, S2.Pin_4, S3.Pin_3, S3.Pin_4
  N5: Part1.D9, S1.Pin_1, S1.Pin_2, R3.Pin_0
  N6: Part1.N$16, 7_Segment3.Segment_D
  N7: Part1.N$17, 7_Segment4.Segment_B
  N8: Part1.N$26, 7_Segment4.Segment_C
  N9: Part1.N$53, Part1.N$117, 7_Segment4.common_anode
  N10: Part1.N$63, 7_Segment2.Segment_C
  N11: Part1.N$64, 7_Segment2.Segment_DP
  N12: Part1.N$76, 7_Segment2.Segment_B
  N13: Part1.N$77, 7_Segment2.Segment_A
  N14: Part1.N$93, 7_Segment4.Segment_G
  N15: Part1.N$118, Part1.N$271, 7_Segment2.common_anode
  N16: Part1.N$235, 7_Segment1.Segment_DP
  N17: Part1.N$251, 7_Segment2.Segment_D
  N18: Part1.N$252, 7_Segment2.Segment_E
  N19: Part1.N$259, 7_Segment1.Segment_B
  N20: Part1.N$263, 7_Segment1.Segment_F
  N21: Part1.N$267, 7_Segment3.Segment_DP
  N22: Part1.N$268, 7_Segment1.Segment_D
  N23: Part1.N$272, 7_Segment2.Segment_F
  N24: Part1.N$273, 7_Segment2.Segment_G
  N25: Part1.N$282, 7_Segment1.Segment_G
  N26: Part1.N$295, 7_Segment3.Segment_A
  N27: Part1.N$298, 7_Segment3.Segment_B
  N28: Part1.N$304, 7_Segment4.Segment_DP
  N29: Part1.N$314, 7_Segment1.Segment_A
  N30: Part1.N$318, 7_Segment3.Segment_G
  N31: Part1.N$319, 7_Segment3.Segment_F
  N32: Part1.N$381, 7_Segment4.Segment_A
  N33: Part1.N$385, 7_Segment4.Segment_F
  N34: Part1.N$393, 7_Segment4.Segment_E
  N35: Part1.N$396, 7_Segment4.Segment_D
